# Fritzing sketch edison_debug (saved by Fritzing 0.9.2b)
breadboards: 1

parts:
  Part1 = Arduino Uno (Rev3)
  IR1 = TSOP312.., 314.. [package=THT]

nets:
  N1: Part1.D13/SCK, IR1.GND
  N2: Part1.5V, IR1.Data
  N3: Part1.GND, IR1.Vs
